# Fritzing sketch pcb (saved by Fritzing 0.9.5d)
circuit board: 8.41461cm x 4.34637cm
breadboards: 1

parts:
  DFRobot_DFPlayer_Mini1 = DFRobot DFPlayer Mini [part_number=DFR0299]
  WeMos_D1_Mini1 = WeMos D1 Mini
  ZS-042_RTC1 = ZS-042 RTC Module
  C1 = Electrolytic Capacitor [capacitance=1µF package="100 mil [THT, electrolytic]"]
  SPKR = female pin header, 2 pins [form="♀ (female)"]

nets:
  VCC: DFRobot_DFPlayer_Mini1.VCC, WeMos_D1_Mini1.5V, ZS-042_RTC1.VCC, C1.+
  N1: DFRobot_DFPlayer_Mini1.RX, WeMos_D1_Mini1.D5
  N2: DFRobot_DFPlayer_Mini1.TX, WeMos_D1_Mini1.D1
  N3: DFRobot_DFPlayer_Mini1.SPK_1, SPKR.pin2
  N4: DFRobot_DFPlayer_Mini1.GND-1, DFRobot_DFPlayer_Mini1.GND-2, WeMos_D1_Mini1.G, ZS-042_RTC1.GND, C1.-
  N5: DFRobot_DFPlayer_Mini1.SPK_2, SPKR.pin1
  N6: WeMos_D1_Mini1.D0, WeMos_D1_Mini1.RST
  N7: WeMos_D1_Mini1.D6, ZS-042_RTC1.SDA
  N8: WeMos_D1_Mini1.D7, ZS-042_RTC1.SCL

notes:
  Birdnoise - Klucsik K. P.
  speaker
